// Digital circuit Divisor.dig as structural Verilog
module Divisor (
  input  [1:0] x,
  input  [1:0] y,
  output [1:0] cociente,
  output [1:0] residuo,
  output signal
);

  wire and_2_out, and_3_out, and_4_out, and_5_out, and_7_out, and_8_out, and_9_out;

  and and_1 (cociente[1], x[1], ~y[1], y[0]);  // And
  and and_2 (and_2_out, x[0], ~y[1], y[0]);  // And
  and and_3 (and_3_out, x[1], x[0], y[0]);
  and and_4 (and_4_out, x[1], x[0], y[1]);
  and and_5 (and_5_out, x[1], y[1], ~y[0]);  // And
  and and_6 (residuo[1], x[1], ~x[0], y[1], y[0]);  // And
  and and_7 (and_7_out, ~x[1], x[0], y[1]);  // And
  and and_8 (and_8_out, x[0], y[1], ~y[0]);  // And
  and and_9 (and_9_out, x[1], ~x[0], ~y[1], y[0]);  // And
  and and_10 (signal, ~y[1], ~y[0]);  // And
  or or_1 (cociente[0], and_2_out, and_3_out, and_4_out, and_5_out);
  or or_2 (residuo[0], and_7_out, and_8_out, and_9_out);
endmodule

/* Test case:
x y cociente residuo signal
0 0 0 0 1
0 1 0 0 0
0 2 0 0 0
0 3 0 0 0
1 0 0 0 1
1 1 1 0 0
1 2 0 1 0
1 3 0 1 0
2 0 0 0 1
2 1 2 1 0
2 2 1 0 0
2 3 0 2 0
3 0 0 0 1
3 1 3 0 0
3 2 1 1 0
3 3 1 0 0
*/
