// Digital circuit ejercicio1.dig as structural Verilog
module ejercicio1 (
  input  [1:0] a,
  input  [1:0] b,
  output [1:0] q,
  output [1:0] r,
  output inv
);

  Divisor divisor_1 (.x(a), .y(b), .cociente(q), .residuo(r), .signal(inv));
endmodule

/* Test case:
    a   b     q         r        inv
loop(i,4)
    (i) 0     x         x        1
end loop 
loop(i,4)
  loop(j,3)
    (i) (j+1) (i/(j+1)) (i%(j+1)) 0
  end loop
end loop
*/
