// Digital circuit test_5bits.dig as structural Verilog
module test_5bits (
  input  [4:0] n,
  output [4:0] out
);

  wire and_1_out, and_2_out, and_3_out, and_4_out, and_5_out, and_6_out, and_7_out, and_8_out, and_9_out,
       and_10_out, and_11_out, and_12_out, and_13_out, and_14_out, and_15_out, and_16_out;

  and and_1 (and_1_out, n[4], n[0]);
  and and_2 (and_2_out, n[4], n[1], ~n[0]);  // And
  and and_3 (and_3_out, n[4], n[3], ~n[1], ~n[0]);  // And
  and and_4 (and_4_out, n[4], n[2], ~n[1], ~n[0]);  // And
  and and_5 (and_5_out, ~n[4], n[3]);  // And
  and and_6 (and_6_out, n[4], ~n[3], n[1]);  // And
  and and_7 (and_7_out, n[4], ~n[3], ~n[1], n[0]);  // And
  and and_8 (and_8_out, n[4], ~n[3], n[2], ~n[1]);  // And
  and and_9 (and_9_out, n[3], ~n[2], ~n[1], ~n[0]);  // And
  and and_10 (and_10_out, ~n[4], n[2]);  // And
  and and_11 (and_11_out, n[4], ~n[2], n[0]);  // And
  and and_12 (and_12_out, n[4], ~n[2], n[1], ~n[0]);  // And
  and and_13 (and_13_out, n[2], ~n[1], ~n[0]);  // And
  and and_14 (and_14_out, ~n[4], n[1], n[0]);  // And
  and and_15 (and_15_out, n[1], ~n[0]);  // And
  and and_16 (and_16_out, n[4], ~n[1], n[0]);  // And
  or or_1 (out[4], and_1_out, and_2_out, and_3_out, and_4_out);
  or or_2 (out[3], and_5_out, and_6_out, and_7_out, and_8_out, and_9_out);
  or or_3 (out[2], and_10_out, and_11_out, and_12_out, and_13_out);
  or or_4 (out[1], and_14_out, and_15_out, and_16_out);

  assign out[0] = n[0];
endmodule

/* Test case:
n out
1 1
2 2
3 3
4 4
5 5
6 6 
7 7
8 8
9 9
10 10
11 11
12 12
13 13
14 14
15 15
16 0
*/
