// Digital circuit IsPrime.dig as structural Verilog
module IsPrime (
  input  n4,
  input  n3,
  input  n2,
  input  n1,
  input  n0,
  output p
);

  wire and_1_out, and_2_out, and_3_out, and_4_out, and_5_out;

  and and_1 (and_1_out, ~n3, n1, n0);  // And
  and and_2 (and_2_out, n4, ~n3, ~n2, ~n1, n0);  // And
  and and_3 (and_3_out, ~n4, n2, ~n1, n0);  // And
  and and_4 (and_4_out, ~n4, ~n3, ~n2, n1, ~n0);  // And
  and and_5 (and_5_out, n4, n3, n2, n0);
  or or_1 (p, and_1_out, and_2_out, and_3_out, and_4_out, and_5_out);
endmodule

/* Test case:
n4 n3 n2 n1 n0 p
0 0 0 0 0 0
0 0 0 0 1 0
0 0 0 1 0 1
0 0 0 1 1 1
0 0 1 0 0 0 
0 0 1 0 1 1
0 0 1 1 0 0
0 0 1 1 1 1
0 1 0 0 0 0
0 1 0 0 1 0
0 1 0 1 0 0
0 1 0 1 1 0
0 1 1 0 0 0
0 1 1 0 1 1
0 1 1 1 0 0
0 1 1 1 1 0
1 0 0 0 0 0
1 0 0 0 1 1
1 0 0 1 0 0
1 0 0 1 1 1
1 0 1 0 0 0
1 0 1 0 1 0
1 0 1 1 0 0
1 0 1 1 1 1
1 1 0 0 0 0
1 1 0 0 1 0
1 1 0 1 0 0
1 1 0 1 1 0
1 1 1 0 0 0
1 1 1 0 1 1
1 1 1 1 0 0
1 1 1 1 1 1
*/
