// Digital circuit 2-BitsMultiplier.dig as structural Verilog
module _2_BitsMultiplier (
  input  [1:0] x,
  input  [1:0] y,
  output [3:0] out
);

  wire and_2_out, and_3_out, and_4_out, and_5_out, and_6_out, and_7_out;

  and and_1 (out[3], x[1], x[0], y[1], y[0]);
  and and_2 (and_2_out, x[1], y[1], ~y[0]);  // And
  and and_3 (and_3_out, x[1], ~x[0], y[1]);  // And
  and and_4 (and_4_out, x[1], ~y[1], y[0]);  // And
  and and_5 (and_5_out, x[1], ~x[0], y[0]);  // And
  and and_6 (and_6_out, x[0], y[1], ~y[0]);  // And
  and and_7 (and_7_out, ~x[1], x[0], y[1]);  // And
  or or_1 (out[2], and_2_out, and_3_out);
  and and_8 (out[0], x[0], y[0]);
  or or_2 (out[1], and_4_out, and_5_out, and_6_out, and_7_out);
endmodule
