// Digital circuit prueba1_p5_2020.dig as structural Verilog
module prueba1_p5_2020 (
  input  [1:0] x,
  input  [1:0] y,
  output [3:0] p
);

  _2_BitsMultiplier _2_bitsmultiplier_1 (.x(x), .y(y), .out(p));
endmodule

/* Test case:
x y p
loop(a, 4)
    loop(b, 4)
	(a) (b) (a*b)
    end loop
end loop	
*/
