// Digital circuit adder-8bits.dig as structural Verilog
module adder_8bits (
  input  [7:0] x,
  input  [7:0] y,
  output [7:0] sum,
  output cout
);

  wire full_adder_1_cout, full_adder_2_cout, full_adder_3_cout, full_adder_4_cout, full_adder_5_cout,
       full_adder_6_cout, full_adder_7_cout;

  full_adder full_adder_1 (.x(x[0]), .y(y[0]), .cin(1'b0), .sum(sum[0]), .cout(full_adder_1_cout));
  full_adder full_adder_2 (.x(x[1]), .y(y[1]), .cin(full_adder_1_cout), .sum(sum[1]), .cout(full_adder_2_cout));
  full_adder full_adder_3 (.x(x[2]), .y(y[2]), .cin(full_adder_2_cout), .sum(sum[2]), .cout(full_adder_3_cout));
  full_adder full_adder_4 (.x(x[3]), .y(y[3]), .cin(full_adder_3_cout), .sum(sum[3]), .cout(full_adder_4_cout));
  full_adder full_adder_5 (.x(x[4]), .y(y[4]), .cin(full_adder_4_cout), .sum(sum[4]), .cout(full_adder_5_cout));
  full_adder full_adder_6 (.x(x[5]), .y(y[5]), .cin(full_adder_5_cout), .sum(sum[5]), .cout(full_adder_6_cout));
  full_adder full_adder_7 (.x(x[6]), .y(y[6]), .cin(full_adder_6_cout), .sum(sum[6]), .cout(full_adder_7_cout));
  full_adder full_adder_8 (.x(x[7]), .y(y[7]), .cin(full_adder_7_cout), .sum(sum[7]), .cout(cout));
endmodule

/* Test case:
    x y sum
loop(a, 256)
    loop(b, 256)
    (a) (b) (a+b)
    end loop
end loop
*/
