// Digital circuit classexer.dig as structural Verilog
module classexer (
  input  x,
  input  y,
  input  z,
  output out
);

  wire and_1_out, and_2_out, and_3_out, not_1_out, not_2_out, not_3_out;

  not not_1 (not_1_out, x);
  not not_2 (not_2_out, z);
  and and_1 (and_1_out, not_1_out, y, z);
  not not_3 (not_3_out, y);
  and and_2 (and_2_out, x, not_3_out, not_2_out);
  and and_3 (and_3_out, x, y, z);
  or or_1 (out, and_1_out, and_2_out, and_3_out);
endmodule

/* Test case:
x y z out
0 0 0 0
0 0 1 0
0 1 0 0
0 1 1 1
1 0 0 1
1 0 1 0
1 1 0 0
1 1 1 1
*/
