// Digital circuit full-adder.dig as structural Verilog
module full_adder (
  input  x,
  input  y,
  input  cin,
  output sum,
  output cout
);

  wire and_1_out, and_2_out, xor_1_out;

  xor xor_1 (xor_1_out, x, y);
  xor xor_2 (sum, xor_1_out, cin);
  and and_1 (and_1_out, x, y);
  and and_2 (and_2_out, xor_1_out, cin);
  or or_1 (cout, and_1_out, and_2_out);
endmodule
