// Digital circuit led-button.dig as structural Verilog
module led_button (
  input  clk
);

  wire and_1_out, and_2_out, and_3_out, or_1_out, pulsador_out, Q0_q, Q1_q;

  Register Q1 (.D(or_1_out), .C(clk), .en(1'b1), .Q(Q1_q));
  Register Q0 (.D(pulsador_out), .C(clk), .en(1'b1), .Q(Q0_q));
  Button pulsador (.out(pulsador_out));
  and and_1 (and_1_out, ~Q1_q, Q0_q, ~pulsador_out);  // And
  and and_2 (and_2_out, Q1_q, ~Q0_q);  // And
  and and_3 (and_3_out, Q1_q, pulsador_out);
  LED led_1 (.in(Q1_q));
  or or_1 (or_1_out, and_1_out, and_2_out, and_3_out);

  // Notes on the sheet:
  //   clk: Hz: 800
endmodule
