// Digital circuit led-button2.dig as structural Verilog
module led_button2 (
  input  clk
);

  wire multiplexer_5_out, pulsador_out;
  wire [1:0] Estado_Actual_q, multiplexer_1_out, multiplexer_2_out, multiplexer_3_out, multiplexer_4_out,
       multiplexer_6_out;

  Button pulsador (.out(pulsador_out));
  Register #(.Bits(2)) Estado_Actual (.D(multiplexer_6_out), .C(clk), .en(1'b1), .Q(Estado_Actual_q));
  Multiplexer #(.Bits(2)) multiplexer_1 (.sel(pulsador_out), .in_0(2'b00), .in_1(2'b01), .out(multiplexer_1_out));
  Multiplexer #(.Bits(2)) multiplexer_2 (.sel(pulsador_out), .in_0(2'b10), .in_1(2'b01), .out(multiplexer_2_out));
  Multiplexer #(.Bits(2)) multiplexer_3 (.sel(pulsador_out), .in_0(2'b10), .in_1(2'b11), .out(multiplexer_3_out));
  Multiplexer #(.Bits(2)) multiplexer_4 (.sel(pulsador_out), .in_0(2'b00), .in_1(2'b11), .out(multiplexer_4_out));
  Multiplexer #(.Selector_Bits(2)) multiplexer_5 (
    .sel(Estado_Actual_q), .in_0(1'b0), .in_1(1'b0), .in_2(1'b1), .in_3(1'b1), .out(multiplexer_5_out));
  Multiplexer #(.Bits(2), .Selector_Bits(2)) multiplexer_6 (
    .sel(Estado_Actual_q), .in_0(multiplexer_1_out), .in_1(multiplexer_2_out), .in_2(multiplexer_3_out),
    .in_3(multiplexer_4_out), .out(multiplexer_6_out));
  LED led_1 (.in(multiplexer_5_out));

  // Notes on the sheet:
  //   clk: Hz: 800
endmodule
