// Digital circuit led-button3.dig as structural Verilog
module led_button3 (
  input  clk
);

  wire pulsador_out, u_LedButton_led;

  Button pulsador (.out(pulsador_out));
  LedButton #(.applicationType("IVERILOG")) u_LedButton (.clk(clk), .p(pulsador_out), .led(u_LedButton_led));
  LED led_1 (.in(u_LedButton_led));

  // Notes on the sheet:
  //   clk: Hz: 800
endmodule

/* Code of LedButton:
module LedButton (
    input clk,
    input p,
    output reg led
);
    reg [1:0] curr_state;
    // Register  Current State
    reg [1:0] next_state;

    always @ (posedge clk)
        curr_state = next_state;

    // Mux LED Status
    always @ (curr_state)
    begin
        case (curr_state)
            2'd0: led = 1'b0;
            2'd1: led = 1'b0;
            2'd2: led = 1'b1;
            2'd3: led = 1'b1;
        endcase   
    end

    // Muxes Next State
always @ (curr_state or p)
    begin
        case (curr_state)
            2'd0: next_state = p? 2'd1 : 2'd0;
            2'd1: next_state = p? 2'd1 : 2'd2;
            2'd2: next_state = p? 2'd3 : 2'd2;
            2'd3: next_state = p? 2'd3 : 2'd0;
            default:
            next_state = 2'd0;
        endcase   
    end
endmodule
*/
