// Digital circuit nand.dig as structural Verilog
module \nand  (
  input  x,
  input  y,
  output out
);

  wire nfet_1_s;

  PFET pfet_1 (.G(x), .S(1'b1), .D(out));
  PFET pfet_2 (.G(y), .S(1'b1), .D(out));
  NFET nfet_1 (.G(x), .D(out), .S(nfet_1_s));
  NFET nfet_2 (.G(y), .D(nfet_1_s), .S(1'b0));
endmodule

/* Test case:
x y out
0 0 1
0 1 1
1 0 1
1 1 0
*/
