// Digital circuit test1.dig as structural Verilog
module test1 (
  input  x,
  output out
);

  PFET pfet_1 (.G(x), .S(1'b1), .D(out));
  NFET nfet_1 (.G(x), .D(out), .S(1'b0));
endmodule

/* Test case:
x out
0 1
1 0
*/
