// Digital circuit projectV2.dig as structural Verilog
module projectV2 (
  input  clk,
  input  [31:0] metros,
  input  switch,
  output [31:0] total
);

  wire r0, r1, r2, r3, r4, r5, r6, r7, r8, r9, r10, r11, r12, r13, r14, r15, r16, r17, r20, r21, r22, r23,
       r24, r25, r26, r27, r30, r31, r32, r33, r34, r35, r36, r37, r40, r41, r42, r43, r44, r45, r46, r47,
       r50, r51, r52, r53, r54, r55, r56, r57, r60, r61, r62, r63, r64, r65, r66, r67, r70, r71, r72, r73,
       r74, r75, r76, r77, r80, r81, r82, r83, r84, r85, r86, r87, rst;

  Seven_Seg seven_seg_1 (.a(r57), .b(r56), .c(r55), .d(r54), .e(r53), .f(r52), .g(r51), .dp(r50));
  Seven_Seg seven_seg_2 (.a(r67), .b(r66), .c(r65), .d(r64), .e(r63), .f(r62), .g(r61), .dp(r60));
  Seven_Seg seven_seg_3 (.a(r77), .b(r76), .c(r75), .d(r74), .e(r73), .f(r72), .g(r71), .dp(r70));
  Seven_Seg seven_seg_4 (.a(r87), .b(r86), .c(r85), .d(r84), .e(r83), .f(r82), .g(r81), .dp(r80));
  Seven_Seg seven_seg_5 (.a(r17), .b(r16), .c(r15), .d(r14), .e(r13), .f(r12), .g(r11), .dp(r10));
  Button _1 (.out(r1));
  Button _4 (.out(r4));
  Button _7 (.out(r7));
  Button calcular (.out(rst));
  Seven_Seg seven_seg_6 (.a(r27), .b(r26), .c(r25), .d(r24), .e(r23), .f(r22), .g(r21), .dp(r20));
  Button _2 (.out(r2));
  Button _5 (.out(r5));
  Button _8 (.out(r8));
  Button _0 (.out(r0));
  converter #(.applicationType("IVERILOG")) u_converter (
    .clk(clk), .rst(rst), .im(metros), .iop(switch), .result(total),
    .pc1({r17, r16, r15, r14, r13, r12, r11, r10}), .pc2({r27, r26, r25, r24, r23, r22, r21, r20}),
    .pc3({r37, r36, r35, r34, r33, r32, r31, r30}), .pc4({r47, r46, r45, r44, r43, r42, r41, r40}),
    .pn5({r57, r56, r55, r54, r53, r52, r51, r50}), .pn6({r67, r66, r65, r64, r63, r62, r61, r60}),
    .pn7({r77, r76, r75, r74, r73, r72, r71, r70}), .pn8({r87, r86, r85, r84, r83, r82, r81, r80}));
  Seven_Seg seven_seg_7 (.a(r37), .b(r36), .c(r35), .d(r34), .e(r33), .f(r32), .g(r31), .dp(r30));
  Button _3 (.out(r3));
  Button _6 (.out(r6));
  Button _9 (.out(r9));
  Seven_Seg seven_seg_8 (.a(r47), .b(r46), .c(r45), .d(r44), .e(r43), .f(r42), .g(r41), .dp(r40));

  // Other names for the same wires on the sheet: km_ml = switch; mts[31:0] = metros;
  //   tecla[9:0] = {r9, r8, r7, r6, r5, r4, r3, r2, r1, r0}; r18[7:0] = {r17, r16, r15, r14, r13, r12, r11, r10};
  //   r28[7:0] = {r27, r26, r25, r24, r23, r22, r21, r20}; r38[7:0] = {r37, r36, r35, r34, r33, r32, r31, r30};
  //   r48[7:0] = {r47, r46, r45, r44, r43, r42, r41, r40}; r58[7:0] = {r57, r56, r55, r54, r53, r52, r51, r50};
  //   r68[7:0] = {r67, r66, r65, r64, r63, r62, r61, r60}; r78[7:0] = {r77, r76, r75, r74, r73, r72, r71, r70};
  //   r88[7:0] = {r87, r86, r85, r84, r83, r82, r81, r80}; resultado[31:0] = total

  // Notes on the sheet:
  //   clk: Hz: 500
  //   Numero Ingresado
  //   Teclado
  //   Conversion
  //   Circuito
  //   Comprobante de resultado
  //   Conexiones Para Display
endmodule

/* Code of converter:
`define INICIO      4'b0000
`define RESULTADO1  4'b0001
`define INICIARV    4'b0010
`define CONDICION1  4'b0011
`define KILOMETROS  4'b0100
`define MILLAS      4'b0101
`define RESULTADO2  4'b0111
`define FIN         4'b1000

module converter(
    input clk,
    input rst,
    input [31:0] im,
    input iop,
    output reg [31:0]result,
    //Salidas para las 4 pantallas de conversion
    output [7:0] pc1,
    output [7:0] pc2,
    output [7:0] pc3,
    output [7:0] pc4,
    //Salidas para las 4 pantallas del numero
    output [7:0] pn5,
    output [7:0] pn6,
    output [7:0] pn7,
    output [7:0] pn8
);

    reg [3:0] curr_state;
    reg [3:0] next_state;
    reg [31:0] m;
    reg op, nop;
    reg [31:0] nm;
    reg [31:0] nresult;

     drawBits resultado(
        .ingresadoEx(nresult[13:0]), 
        .valor1(pc1), 
        .valor2(pc2), 
        .valor3(pc3), 
        .valor4(pc4));
     
     drawBits numero(   
        .ingresadoEx(im[13:0]), 
        .valor1(pn5), 
        .valor2(pn6), 
        .valor3(pn7), 
        .valor4(pn8));


    //current state
    always @ (posedge clk)
    begin
        if(rst)
            curr_state <= `INICIO;
        else
            curr_state <= next_state; 
    end

    //registers
    always @ (posedge clk)
    begin
        m <= nm;
        op <= nop;
        result <= nresult;
    end

    //next register values
    always @ (*)
    begin
        nm = m;
        
        nresult = result;

        case (curr_state)
            `RESULTADO1: nresult = 32'd0;
            `INICIARV: begin
                nm = im;
            end
            `KILOMETROS: begin
                nm = m / 1000;
            end
            `MILLAS: begin
                nm = m * 0.00062137;
            end
            `RESULTADO2: nresult =  nm;
        endcase
    end

    //next state
    always @ (*)
    begin
        case (curr_state)
        `INICIO:
            if (im == 32'd0)
               next_state = `RESULTADO1;
            else
                next_state = `INICIARV;
        `RESULTADO1:
            next_state = `FIN;
        `INICIARV:
             next_state = `CONDICION1;
        `CONDICION1:
            if (iop == 32'd1)
                next_state = `KILOMETROS;
            else
                next_state = `MILLAS;
        `KILOMETROS:
            next_state = `RESULTADO2;
        `MILLAS:
            next_state = `RESULTADO2;
        `FIN:
            next_state = `FIN;

        endcase

    end

endmodule

module drawBits(
    input [13:0] ingresadoEx,
    output [7:0] valor1,
    output [7:0] valor2,
    output [7:0] valor3,
    output [7:0] valor4
);
    
    reg [13:0] contador, contador2, contador3;
    reg [13:0] comparador;
    reg [13:0] pantalla1;
    reg [13:0] pantalla2;
    reg [13:0] pantalla3;
    reg [13:0] pantalla4;
    
    dTB np1(
        .ingresado(pantalla1), 
        .valorBits(valor1));
    dTB np2(
        .ingresado(pantalla2), 
        .valorBits(valor2));
    dTB np3(
        .ingresado(pantalla3), 
        .valorBits(valor3));
    dTB np4(
        .ingresado(pantalla4), 
        .valorBits(valor4));

//Motivo por el cual no tiene valores flotantes: https://bit.ly/2LJv48F
     always @(*) 
        begin
            comparador = ingresadoEx;
            if (comparador < 10) begin
                pantalla1 = 14'b0;
                pantalla2 = 14'b0;
                pantalla3 = 14'b0;
                pantalla4 = comparador;
            end
            else if(comparador < 100) begin
                contador = 14'b0;
                pantalla1 = 14'b0;
                pantalla2 = 14'b0;
                while (comparador >= 10) 
                begin
                    contador = contador + 4'd1;
                    comparador = comparador - 10;
                end
                pantalla3 = contador;
                pantalla4 = comparador;
            end
            else if (comparador < 1000) begin
                contador = 14'b0;
                contador2 = 14'b0;
                pantalla1 = 14'b0;
                while (comparador >= 100) begin
                    comparador = comparador - 100;
                    contador2 = contador2 + 4'd1;
                end

                while (comparador >= 10) 
                begin
                    contador = contador + 4'd1;
                    comparador = comparador - 10;
                end
                pantalla2 = contador2;
                pantalla3 = contador;
                pantalla4 = comparador;
            end 
            else
            begin
                contador = 14'b0;
                contador2 = 14'b0;
                contador3 = 14'b0;

                while (comparador >= 1000) begin 
                    comparador = comparador - 1000;
                    contador3 = contador3 + 4'd1;
                end

                while (comparador >= 100) begin
                    comparador = comparador - 100;
                    contador2 = contador2 + 4'd1;
                end

                while (comparador >= 10) 
                begin
                    contador = contador + 4'd1;
                    comparador = comparador - 10;
                end
                pantalla1 = contador3;
                pantalla2 = contador2;
                pantalla3 = contador;
                pantalla4 = comparador;
            end      
           
        end
        

endmodule


//Simulacion de decoder ¿como lo hice? : https://bit.ly/2WtoPs0
//¿Como se donde van los segmentos? : https://bit.ly/37ue52z
module dTB(
        input [13:0] ingresado,
        output [7:0] valorBits
        );

        reg [7:0] screen;
        assign valorBits = screen;
        
        always @ (*)
        begin
            if(ingresado == 0)begin
                screen <= 8'b11111100;
            end
            else if(ingresado == 1)begin
                screen <= 8'b01100000;
            end
            else if (ingresado == 2) begin
                screen <= 8'b11011010;
            end
            else if (ingresado == 3) begin
                screen <= 8'b11110010;
            end
            else if (ingresado == 4) begin
                screen <= 8'b01100110;
            end
            else if (ingresado == 5) begin
                screen <= 8'b10110110;
            end
            else if (ingresado == 6) begin
                screen <= 8'b00111110;
            end
            else if (ingresado == 7) begin
                screen <= 8'b11100000;
            end
            else if (ingresado == 8) begin
                screen <= 8'b11111110;
            end
            else if (ingresado == 9) begin
                screen <= 8'b11100110;
            end
            else
            begin
                screen <= 8'b00000000;
            end
            
        end

    endmodule
*/
