// Digital circuit full-adder.dig as structural Verilog
module full_adder (
  input  a,
  input  b,
  input  cin,
  output sum,
  output cout
);

  FullAdder #(.applicationType("IVERILOG")) u_FullAdder (.a(a), .b(b), .cin(cin), .sum(sum), .cout(cout));
endmodule

/* Code of FullAdder:
module FullAdder (
    input a,
    input b,
    input cin,
    output sum,
    output cout
);
    assign sum = a ^ b ^ cin;
    assign cout = (a ^ b) & cin | a & b;
endmodule
*/
